# Fritzing sketch ESP8266TrafficLight (saved by Fritzing 0.9.3b)
breadboards: 2

parts:
  WeMos_D1_Mini3 = WeMos D1 Mini  # not connected
  LED1 = LED - 3mm [color="Red (633nm)" package="3 mm [THT]"]
  LED2 = LED - 3mm [color="Yellow (592nm)" package="3 mm [THT]"]
  R1 = Resistor [tolerance=±5% resistance=220 package="0603 [SMD]"]
  R2 = Resistor [tolerance=±5% resistance=1k package="0603 [SMD]"]
  LED3 = LED - 3mm [color="Green (565nm)" package="3 mm [THT]"]
  R3 = Resistor [tolerance=±5% resistance=470 package="0603 [SMD]"]

nets:
  N1: LED1.anode, R2.Pin_0
  N2: LED2.anode, R3.Pin_0
  N3: R1.Pin_0, LED3.anode
  N4: R1.Pin_1, R2.Pin_1, R3.Pin_1
